# Fritzing sketch pcb (saved by Fritzing 0.9.4)
circuit board: 6.11104cm x 4.56963cm
breadboards: 1

parts:
  J1 = female pin header, 18 pins [form="♀ (female)"]  # not connected
  J2 = female pin header, 24 pins [form="♀ (female)"]  # not connected
  J3 = female pin header, 8 pins [form="♀ (female)"]
  J4 = female pin header, 8 pins [form="♀ (female)"]
  IC1 = IC, DIP package, 14 pins [chip_label=IC]
  APA102 = female pin header, 4 pins [form="♀ (female)"]
  Q1 = Basic FET N-Channel [package="TO220 [THT]"]
  R1 = Resistor [tolerance=±5% resistance=220 package=THT]
  R2 = Resistor [tolerance=±5% resistance=220 package=THT]

nets:
  GND: J3.pin6, IC1.pin7, IC1.pin9, IC1.pin10, IC1.pin12, IC1.pin13, Q1.source, R2.Pin_1
  5V: J3.pin7, IC1.pin14, APA102.pin1
  GPIO17: J4.pin2, IC1.pin1, IC1.pin4, R1.Pin_1
  GPIO18: J4.pin4, IC1.pin2
  GPIO23: J4.pin5, IC1.pin5
  CI: IC1.pin3, APA102.pin4
  DI: IC1.pin6, APA102.pin3
  ledGND: APA102.pin2, Q1.drain
  N1: Q1.gate, R1.Pin_0, R2.Pin_0
