# Fritzing sketch pcb2 (saved by Fritzing 0.9.4)
circuit board: 6.11104cm x 4.56963cm
breadboards: 1

parts:
  IC1 = IC, DIP package, 14 pins [chip_label=IC]
  Q1 = Basic FET N-Channel [package="TO220 [THT]"]
  R1 = Resistor [tolerance=±5% resistance=220 package=THT]
  R2 = Resistor [tolerance=±5% resistance=220 package=THT]
  HALL = female pin header, 3 pins [form="♀ (female)"]
  APA102 = female pin header, 4 pins [form="♀ (female)"]
  C2 = Ceramic Capacitor [capacitance=100nF package="100 mil [THT, multilayer]"]
  C3 = Electrolytic Capacitor [capacitance=1µF package="100 mil [THT, electrolytic]"]
  Power = female pin header, 2 pins [form="♀ (female)"]
  ESP-R = female pin header, 7 pins [form="♀ (female)"]  # not connected
  ESP-L = female pin header, 7 pins [form="♀ (female)"]
  J4 = female pin header, 2 pins [form="♀ (female)"]

nets:
  OE: IC1.pin1, IC1.pin4, R1.Pin_1, ESP-L.pin7
  MOSI: IC1.pin2, ESP-L.pin3
  DI: IC1.pin3, APA102.pin3
  SCK: IC1.pin5, ESP-L.pin5
  CI: IC1.pin6, APA102.pin2
  GND: IC1.pin7, IC1.pin9, IC1.pin10, IC1.pin12, IC1.pin13, Q1.source, R2.Pin_1, C2.1, C3.-, Power.pin2, J4.pin2
  5V: IC1.pin14, HALL.pin1, APA102.pin4, C2.0, C3.+, Power.pin1, J4.pin1
  N1: Q1.gate, R1.Pin_0, R2.Pin_0
  ledGND: Q1.drain, HALL.pin2, APA102.pin1
  HALL: HALL.pin3, ESP-L.pin1
